// Logisim project Oblig1.circ as structural Verilog: 1 circuit, main circuit main
module main (
  input  in_1,
  input  A3,
  input  in_3,
  input  A1,
  input  A0,
  output out_6,
  output out_7,
  output out_8,
  output out_9,
  output out_10,
  output out_11,
  output out_12,
  output out_13
);

  wire and_2_out, and_3_out, and_4_out, xor_3_out;

  and and_1 (out_6, A3, and_2_out);
  and and_2 (and_2_out, in_3, and_3_out);
  xor xor_1 (out_7, A3, and_2_out);
  xor xor_2 (out_8, in_3, and_3_out);
  and and_3 (and_3_out, A1, A3);
  xor xor_3 (xor_3_out, A1, A3);
  xor xor_4 (out_9, xor_3_out, and_4_out);
  and and_4 (and_4_out, in_3, A0);
  xor xor_5 (out_10, A0, in_3);

  assign out_11 = A1;
  assign out_12 = A0;

  // Notes on the sheet:
  //   A2
endmodule
