// Logisim project healthy.circ as structural Verilog: 6 circuits, main circuit main
module main (
  output [7:0] out_1
);

  wire and_1_out, button_1_out, button_2_out, dekoder_1_aaaa, dekoder_1_data_lsb, dekoder_1_data_msb,
       dekoder_1_load, not_1_out, not_2_out, or_1_out;
  wire [3:0] counter_out_3;
  wire [7:0] controlled_buffer_1_out, n2x4_tristate_1_out_5, ram_1_data, register_1_q, rom_1_data;

  Button button_1 (.out(button_1_out));
  Button button_2 (.out(button_2_out));
  counter counter (.in_1(button_1_out), .out_3(counter_out_3), .in_2(button_2_out));
  Hex_Digit_Display hex_digit_display_1 (.value(counter_out_3));  // open: dp
  ROM #(.addrWidth(4)) rom_1 (.addr(counter_out_3), .data(rom_1_data));  // open: sel
  _8bit_mux u_8bit_mux_1 (
    .input_1(n2x4_tristate_1_out_5), .input_2(controlled_buffer_1_out), .\output (out_1),
    .in_3(dekoder_1_load));
  dekoder dekoder_1 (
    .signal_in(rom_1_data[7:4]), .data_lsb(dekoder_1_data_lsb), .data_msb(dekoder_1_data_msb),
    .load(dekoder_1_load), .aaaa(dekoder_1_aaaa));
  Register #(.trigger("falling")) register_1 (
    .D(out_1), .Q(register_1_q), .clk(or_1_out), .clr(button_2_out));  // open: en
  or or_1 (or_1_out, button_1_out, button_2_out);
  _2x4_tristate u_2x4_tristate_1 (
    .in(rom_1_data[3:0]), .in_4(register_1_q), .lsb(dekoder_1_data_lsb), .out_5(n2x4_tristate_1_out_5),
    .msb(dekoder_1_data_msb));
  assign controlled_buffer_1_out = not_2_out ? ram_1_data : 8'bz;  // Controlled_Buffer controlled_buffer_1
  RAM #(.addrWidth(4), .bus("asynch")) ram_1 (
    .addr(rom_1_data[3:0]), .data(ram_1_data), .ld(not_1_out), .clr(button_2_out));  // open: sel
  assign ram_1_data = dekoder_1_aaaa ? register_1_q : 8'bz;  // Controlled_Buffer controlled_buffer_2
  not not_1 (not_1_out, and_1_out);
  and and_1 (and_1_out, dekoder_1_aaaa, button_1_out);
  not not_2 (not_2_out, dekoder_1_aaaa);

  // Notes on the sheet:
  //   count
  //   clear
  //   clock
  //   instruks rom
  //   controller unit
  //   load
  //   contents of rom_1 (hex, n*v repeats v):
  //   8c 9d b0 b3 81 91 a0 b4
  //   instrukser
  //   data forgrener
  //   data inn
  //   data ut
endmodule

module counter (
  input  in_1,
  input  in_2,
  output [3:0] out_3
);

  wire adder_1_cout, and_1_out, not_1_out;
  wire [3:0] adder_1_out;

  Register #(.width(4), .trigger("falling")) register_1 (
    .D(adder_1_out), .Q(out_3), .clk(and_1_out), .clr(in_2));  // open: en
  and and_1 (and_1_out, in_1, not_1_out);
  not not_1 (not_1_out, adder_1_cout);
  Adder #(.width(4)) adder_1 (.a(out_3), .b(4'b0001), .out(adder_1_out), .cout(adder_1_cout));  // open: cin
endmodule

// some thing
module _2x4_tristate (
  input  lsb,
  input  msb,
  input  [3:0] in,
  input  [7:0] in_4,
  output [7:0] out_5
);

  wire nor_1_out;

  assign out_5 = lsb ? {in_4[7:4], in} : 8'bz;  // Controlled_Buffer controlled_buffer_1
  assign out_5 = msb ? {in, in_4[3:0]} : 8'bz;  // Controlled_Buffer controlled_buffer_2
  assign out_5 = nor_1_out ? in_4 : 8'bz;  // Controlled_Buffer controlled_buffer_3
  nor nor_1 (nor_1_out, lsb, msb);

  // Notes on the sheet:
  //   register input
  //   out
endmodule

// SChmux
module _8bit_mux (
  input  [7:0] input_1,
  input  [7:0] input_2,
  input  in_3,
  output [7:0] \output 
);

  wire not_1_out;

  assign \output  = not_1_out ? input_1 : 8'bz;  // Controlled_Buffer controlled_buffer_1
  assign \output  = in_3 ? input_2 : 8'bz;  // Controlled_Buffer controlled_buffer_2
  not not_1 (not_1_out, in_3);
endmodule

module instrukser (
  input  [3:0] in_1,
  input  in_2,
  output [7:0] out_3
);

  ROM #(.addrWidth(4)) rom_1 (.addr(in_1), .data(out_3), .sel(in_2));
endmodule

module dekoder (
  input  [3:0] signal_in,
  output data_lsb,
  output data_msb,
  output load,
  output aaaa
);

  wire not_1_out, not_2_out, not_3_out, not_4_out;

  not not_1 (not_1_out, signal_in[2]);
  not not_2 (not_2_out, signal_in[1]);
  and and_1 (data_lsb, not_1_out, not_2_out, signal_in[3], not_3_out);
  not not_3 (not_3_out, signal_in[0]);
  and and_2 (data_msb, not_1_out, signal_in[0], not_2_out, signal_in[3]);
  and and_3 (load, signal_in[1], not_1_out, signal_in[3], not_4_out);
  not not_4 (not_4_out, signal_in[0]);
  and and_4 (aaaa, not_1_out, signal_in[0], signal_in[3], signal_in[1]);

  // Notes on the sheet:
  //   dddd
  //   dddd
  //   aaaa
endmodule
